// Logisim project pc_increment_logic.circ as structural Verilog: 1 circuit, main circuit main
module main (
  input  [3:0] pc_increment_by_1,
  input  [3:0] ifun,
  input  [3:0] icode
);

  wire comparator_1_eq;

  Multiplexer #(.width(4), .enable("false")) multiplexer_1 (
    .in0(pc_increment_by_1), .in1(ifun), .sel(comparator_1_eq));  // open: out
  Comparator #(.width(4)) comparator_1 (.a(icode), .b(4'b1001), .eq(comparator_1_eq));  // open: gt, lt
endmodule
